// Logisim project Computer.circ as structural Verilog: 4 circuits, main circuit main
module main (
  input  HLT,
  output CLK,
  output nCLK,
  output PS_ON,
  output RST
);

  wire button_1_out, button_2_out, CLK_HS_out, CLK_LS_out, clock_control_1_halt, clock_control_1_nauto_hs,
       clock_control_1_nauto_ls, clock_control_1_nmanual, Mode_SW_out, not_1_out, Pulse_SW_out;

  Button button_1 (.out(button_1_out));
  Button button_2 (.out(button_2_out));
  Power___Pwr_On power_pwr_on_1 (.SW2(button_1_out), .nPS_ON(PS_ON));
  not not_1 (not_1_out, PS_ON);
  Power___Reset power_reset_1 (.SW(button_2_out), .PWR_OK(not_1_out), .RST(RST));
  Clock #(.highDuration(5), .lowDuration(5)) CLK_LS (.out(CLK_LS_out));
  Clock CLK_HS (.out(CLK_HS_out));
  Button Mode_SW (.out(Mode_SW_out));
  Button Pulse_SW (.out(Pulse_SW_out));
  Clock_Control clock_control_1 (
    .CLK_LS(CLK_LS_out), .CLK_HS(CLK_HS_out), .Mode_sw(Mode_SW_out), .Pulse_sw(Pulse_SW_out), .RST(RST),
    .HLT(HLT), .CLK(CLK), .nCLK(nCLK), .nManual(clock_control_1_nmanual),
    .nAuto_LS(clock_control_1_nauto_ls), .nAuto_HS(clock_control_1_nauto_hs), .Halt(clock_control_1_halt));
  LED Manual (.in(clock_control_1_nmanual));
  LED Auto_LS (.in(clock_control_1_nauto_ls));
  LED Auto_HS (.in(clock_control_1_nauto_hs));
  LED Halt (.in(clock_control_1_halt));

  // Notes on the sheet:
  //   Power - PWR-ON
  //   Power - Reset
  //   Clock Control
endmodule

module Clock_Control (
  input  CLK_LS,
  input  CLK_HS,
  input  Mode_sw,
  input  Pulse_sw,
  input  RST,
  input  HLT,
  output CLK,
  output nCLK,
  output nManual,
  output nAuto_LS,
  output nAuto_HS,
  output Halt
);

  wire C0, C1, CLK_HLT, CLK_INT, CLK_NOT_HLT, MODE_RST, MODE_TRG, nCLK_HLT, nHLT, nMODE0, nMODE1, nMODE2,
       nMODE_RST, nRST, or_1_out, PULSE_TRG;
  wire [1:1] undriven, undriven_2, xl74ls139_1_y0, xl74ls139_1_y1, xl74ls139_1_y2, xl74ls139_1_y3;
  wire [2:0] xl74ls08_1_y;
  wire [3:2] mc14490dwg_1_out, sn74ls193dr_1_out_7;
  wire [3:3] undriven_3, undriven_4, xl74ls00_1_y;

  or or_1 (or_1_out, MODE_RST, RST);
  MC14490DWG mc14490dwg_1 (
    .In({2'b00, Mode_sw, Pulse_sw}), .OSC_In(1'b1), .Out({mc14490dwg_1_out, MODE_TRG, PULSE_TRG}));  // open: OSC_OUT
  SN74LS193DR sn74ls193dr_1 (
    .D(4'b1111), .MR(or_1_out), .nPL(nRST), .CPD(1'b1), .CPU(MODE_TRG), .out_7({sn74ls193dr_1_out_7, C1, C0}));  // open: nTCD, nTCU
  XL74LS04 xl74ls04_1 (
    .A({HLT, nMODE_RST, nMODE2, nMODE1, nMODE0, RST}), .Y({nHLT, MODE_RST, nAuto_HS, nAuto_LS, nManual, nRST}));
  XL74LS139 xl74ls139_1 (
    .nG(2'b00), .A({undriven[1], C0}), .B({undriven_2[1], C1}), .Y0({xl74ls139_1_y0[1], nMODE0}),
    .Y1({xl74ls139_1_y1[1], nMODE1}), .Y2({xl74ls139_1_y2[1], nMODE2}), .Y3({xl74ls139_1_y3[1], nMODE_RST}));
  or or_2 (CLK, CLK_HLT, CLK_NOT_HLT);
  XL74LS00 xl74ls00_1 (
    .A({undriven_3[3], CLK, nCLK_HLT, PULSE_TRG}), .B({undriven_4[3], CLK, nCLK_HLT, HLT}),
    .Y({xl74ls00_1_y[3], nCLK, CLK_HLT, nCLK_HLT}));
  XL74LS08 xl74ls08_1 (
    .A({nHLT, nAuto_HS, nAuto_LS, nManual}), .B({CLK_INT, CLK_HS, CLK_LS, PULSE_TRG}),
    .Y({CLK_NOT_HLT, xl74ls08_1_y}));
  or or_3 (CLK_INT, xl74ls08_1_y[0], xl74ls08_1_y[1], xl74ls08_1_y[2]);

  assign Halt = HLT;

  // Other names for the same wires on the sheet: MODE0 = nManual; MODE1 = nAuto_LS; MODE2 = nAuto_HS
endmodule

module Power___Pwr_On (
  input  SW2,
  output nPS_ON
);

  wire [1:0] n74hc74_653_1_q;
  wire [1:1] lp3470a293dbvr_1_rst_num, n74hc74_653_1_q_num;

  LP3470A293DBVR lp3470a293dbvr_1 (.RST_num(lp3470a293dbvr_1_rst_num[1]));
  _74HC74_653 u_74hc74_653_1 (
    .CP({1'b0, SW2}), .D(2'b01), .SD_num(2'b11), .RD_num({2{lp3470a293dbvr_1_rst_num[1]}}),
    .Q(n74hc74_653_1_q), .Q_num({n74hc74_653_1_q_num[1], nPS_ON}));
endmodule

module Power___Reset (
  input  SW,
  input  PWR_OK,
  output RST
);

  wire [0:0] lp3470a293dbvr_1_rst_num;
  wire [5:0] xl74ls04_1_y;

  LP3470A293DBVR lp3470a293dbvr_1 (.RST_num(lp3470a293dbvr_1_rst_num[0]));
  XL74LS04 xl74ls04_1 (.A({4'b0000, PWR_OK, lp3470a293dbvr_1_rst_num[0]}), .Y(xl74ls04_1_y));
  or or_1 (RST, SW, xl74ls04_1_y[0], xl74ls04_1_y[1]);
endmodule
